// Logisim project qtictactoe.circ as structural Verilog: 24 circuits, main circuit main
module main (
);

  wire engine_1_draw, engine_1_over, engine_1_p1_turn, engine_1_p1_won, engine_1_p2_turn, engine_1_p2_won,
       P2_is_out, RESET_out, t_ff_1_q, t_ff_1_qn, t_ff_2_q, t_ff_2_qn, Who_starts_out;
  wire [8:0] button_2_out, engine_1_board_p1, engine_1_board_p2;

  LED P2 (.in(t_ff_1_q));
  LED P1 (.in(t_ff_1_qn));
  Button Who_starts (.out(Who_starts_out));
  LED Computer (.in(t_ff_2_q));
  LED Player (.in(t_ff_2_qn));
  Button P2_is (.out(P2_is_out));
  Button RESET (.out(RESET_out));
  Button button_1 (.out(button_2_out[1]));
  Button button_2 (.out(button_2_out[0]));
  Button button_3 (.out(button_2_out[4]));
  Button button_4 (.out(button_2_out[3]));
  Button button_5 (.out(button_2_out[7]));
  Button button_6 (.out(button_2_out[6]));
  Button button_7 (.out(button_2_out[2]));
  Button button_8 (.out(button_2_out[5]));
  Button button_9 (.out(button_2_out[8]));
  T_Flip_Flop t_ff_1 (.clk(Who_starts_out), .T(1'b1), .Q(t_ff_1_q), .Qn(t_ff_1_qn));  // open: preset, reset, en
  T_Flip_Flop t_ff_2 (.clk(P2_is_out), .T(1'b1), .Q(t_ff_2_q), .Qn(t_ff_2_qn));  // open: preset, reset, en
  LED P1_TURN (.in(engine_1_p1_turn));
  LED P2_TURN (.in(engine_1_p2_turn));
  LED OVER (.in(engine_1_over));
  ENGINE engine_1 (
    .P2_is_starting(t_ff_1_q), .isComputer(t_ff_2_q), .RESET(RESET_out), .MOV_SLCT_INPUT(button_2_out),
    .P1_TURN(engine_1_p1_turn), .P2_TURN(engine_1_p2_turn), .OVER(engine_1_over), .P1_WON(engine_1_p1_won),
    .P2_WON(engine_1_p2_won), .DRAW(engine_1_draw), .BOARD_P1(engine_1_board_p1), .BOARD_P2(engine_1_board_p2));
  LED P1_WON (.in(engine_1_p1_won));
  LED P2_WON (.in(engine_1_p2_won));
  LED DRAW (.in(engine_1_draw));
  LED led_1 (.in(engine_1_board_p1[0]));
  LED led_2 (.in(engine_1_board_p1[3]));
  LED led_3 (.in(engine_1_board_p1[6]));
  LED led_4 (.in(engine_1_board_p2[0]));
  LED led_5 (.in(engine_1_board_p2[3]));
  LED led_6 (.in(engine_1_board_p2[6]));
  LED led_7 (.in(engine_1_board_p1[1]));
  LED led_8 (.in(engine_1_board_p2[1]));
  LED led_9 (.in(engine_1_board_p1[4]));
  LED led_10 (.in(engine_1_board_p2[4]));
  LED led_11 (.in(engine_1_board_p2[7]));
  LED led_12 (.in(engine_1_board_p1[7]));
  LED led_13 (.in(engine_1_board_p2[2]));
  LED led_14 (.in(engine_1_board_p1[2]));
  LED led_15 (.in(engine_1_board_p2[5]));
  LED led_16 (.in(engine_1_board_p1[5]));
  LED led_17 (.in(engine_1_board_p2[8]));
  LED led_18 (.in(engine_1_board_p1[8]));

  // Notes on the sheet:
  //   IMPORTANT: START SIMULATION!
  //   Make sure tick frequency is >128hz
  //   (Simulate->Tick Frequency)
  //   Make sure ticks are enabled
  //   (Simulate->Ticks Enabled)
  //   Make sure simulation is enabled
  //   (Simulate->Simulation Enabled)
endmodule

module ENGINE (
  input  P2_is_starting,
  input  isComputer,
  input  RESET,
  input  [8:0] MOV_SLCT_INPUT,
  output P1_TURN,
  output P2_TURN,
  output OVER,
  output P1_WON,
  output P2_WON,
  output DRAW,
  output [8:0] BOARD_P1,
  output [8:0] BOARD_P2
);

  wire CLK, p_mov_ok_1_player_move_ok, state_machine_1_p1_write_enable, state_machine_1_p2_write_enable;
  wire [8:0] cpu_1_cpu, p2_switch_1_out;

  Clock clock_1 (.out(CLK));
  STATE_MACHINE state_machine_1 (
    .CLK(CLK), .Player_Move_OK(p_mov_ok_1_player_move_ok), .P2_is_CPU(isComputer),
    .P2_Starts(P2_is_starting), .GameOver(OVER), .RESET(RESET), .P1_Turn(P1_TURN), .P2_Turn(P2_TURN),
    .P1_Write_Enable(state_machine_1_p1_write_enable), .P2_Write_Enable(state_machine_1_p2_write_enable));
  P2_SWITCH p2_switch_1 (.PLR_MOV(MOV_SLCT_INPUT), .CPU_MOV(cpu_1_cpu), .doAI(isComputer), .OUT(p2_switch_1_out));
  BOARD_MEM board_mem_1 (
    .RESET(RESET), .EN(state_machine_1_p1_write_enable), .CLK(CLK), .INP(MOV_SLCT_INPUT), .STATE(BOARD_P1));
  BOARD_MEM board_mem_2 (
    .RESET(RESET), .EN(state_machine_1_p2_write_enable), .CLK(CLK), .INP(p2_switch_1_out), .STATE(BOARD_P2));
  END_DTCT end_dtct_1 (.P1(BOARD_P1), .P2(BOARD_P2), .P1_WIN(P1_WON), .P2_WIN(P2_WON), .DRAW(DRAW), .GAME_OVER(OVER));
  P_MOV_OK p_mov_ok_1 (
    .B1_state(BOARD_P1), .B2_state(BOARD_P2), .pmov(MOV_SLCT_INPUT),
    .Player_Move_OK(p_mov_ok_1_player_move_ok));
  CPU cpu_1 (.P1(BOARD_P1), .P2(BOARD_P2), .CPU(cpu_1_cpu));

  // Other names for the same wires on the sheet: RST = RESET
endmodule

module MOV_SELECT_MEM (
  input  [8:0] INPUT,
  output [8:0] OUTPUT
);

  wire or_1_out, or_2_out, or_3_out, or_4_out, or_5_out, or_6_out, or_7_out, or_8_out, or_9_out;

  or or_1 (or_1_out, INPUT[1], INPUT[2], INPUT[3], INPUT[4], INPUT[5], INPUT[6], INPUT[7], INPUT[8], 1'b0);
  or or_2 (or_2_out, INPUT[0], INPUT[1], INPUT[2], INPUT[4], INPUT[5], INPUT[6], INPUT[7], INPUT[8], 1'b0);
  or or_3 (or_3_out, INPUT[0], INPUT[1], INPUT[2], INPUT[3], INPUT[4], INPUT[5], INPUT[7], INPUT[8], 1'b0);
  or or_4 (or_4_out, INPUT[0], INPUT[2], INPUT[3], INPUT[4], INPUT[5], INPUT[6], INPUT[7], INPUT[8], 1'b0);
  or or_5 (or_5_out, INPUT[0], INPUT[1], INPUT[2], INPUT[3], INPUT[5], INPUT[6], INPUT[7], INPUT[8], 1'b0);
  or or_6 (or_6_out, INPUT[0], INPUT[1], INPUT[2], INPUT[3], INPUT[4], INPUT[5], INPUT[6], INPUT[8], 1'b0);
  or or_7 (or_7_out, INPUT[0], INPUT[1], INPUT[3], INPUT[4], INPUT[5], INPUT[6], INPUT[7], INPUT[8], 1'b0);
  or or_8 (or_8_out, INPUT[0], INPUT[1], INPUT[2], INPUT[3], INPUT[4], INPUT[6], INPUT[7], INPUT[8], 1'b0);
  or or_9 (or_9_out, INPUT[0], INPUT[1], INPUT[2], INPUT[3], INPUT[4], INPUT[5], INPUT[6], INPUT[7], 1'b0);
  S_R_Flip_Flop #(.trigger("high")) s_r_ff_1 (
    .S(INPUT[0]), .clk(1'b1), .R(or_1_out), .Q(OUTPUT[0]));  // open: Qn, preset, reset, en
  S_R_Flip_Flop #(.trigger("high")) s_r_ff_2 (
    .S(INPUT[3]), .clk(1'b1), .R(or_2_out), .Q(OUTPUT[3]));  // open: Qn, preset, reset, en
  S_R_Flip_Flop #(.trigger("high")) s_r_ff_3 (
    .S(INPUT[6]), .clk(1'b1), .R(or_3_out), .Q(OUTPUT[6]));  // open: Qn, preset, reset, en
  S_R_Flip_Flop #(.trigger("high")) s_r_ff_4 (
    .S(INPUT[1]), .clk(1'b1), .R(or_4_out), .Q(OUTPUT[1]));  // open: Qn, preset, reset, en
  S_R_Flip_Flop #(.trigger("high")) s_r_ff_5 (
    .S(INPUT[4]), .clk(1'b1), .R(or_5_out), .Q(OUTPUT[4]));  // open: Qn, preset, reset, en
  S_R_Flip_Flop #(.trigger("high")) s_r_ff_6 (
    .S(INPUT[7]), .clk(1'b1), .R(or_6_out), .Q(OUTPUT[7]));  // open: Qn, preset, reset, en
  S_R_Flip_Flop #(.trigger("high")) s_r_ff_7 (
    .S(INPUT[2]), .clk(1'b1), .R(or_7_out), .Q(OUTPUT[2]));  // open: Qn, preset, reset, en
  S_R_Flip_Flop #(.trigger("high")) s_r_ff_8 (
    .S(INPUT[5]), .clk(1'b1), .R(or_8_out), .Q(OUTPUT[5]));  // open: Qn, preset, reset, en
  S_R_Flip_Flop #(.trigger("high")) s_r_ff_9 (
    .S(INPUT[8]), .clk(1'b1), .R(or_9_out), .Q(OUTPUT[8]));  // open: Qn, preset, reset, en

  // Other names for the same wires on the sheet: MOVSEL_0 = INPUT[0]; MOVSEL_1 = INPUT[1]; MOVSEL_2 = INPUT[2];
  //   MOVSEL_3 = INPUT[3]; MOVSEL_4 = INPUT[4]; MOVSEL_5 = INPUT[5]; MOVSEL_6 = INPUT[6]; MOVSEL_7 = INPUT[7];
  //   MOVSEL_8 = INPUT[8]
endmodule

module BOARD_MEM (
  input  RESET,
  input  EN,
  input  CLK,
  input  [8:0] INP,
  output [8:0] STATE
);

  wire [8:0] or_1_out;

  assign or_1_out = INP | STATE;  // OR_Gate or_1, 9 bits wide
  BOARD_MEM_CELL board_mem_cell_1 (.EN(EN), .D(or_1_out[0]), .CLK(CLK), .RST(RESET), .Q(STATE[0]));
  BOARD_MEM_CELL board_mem_cell_2 (.EN(EN), .D(or_1_out[3]), .CLK(CLK), .RST(RESET), .Q(STATE[3]));
  BOARD_MEM_CELL board_mem_cell_3 (.EN(EN), .D(or_1_out[6]), .CLK(CLK), .RST(RESET), .Q(STATE[6]));
  BOARD_MEM_CELL board_mem_cell_4 (.EN(EN), .D(or_1_out[1]), .CLK(CLK), .RST(RESET), .Q(STATE[1]));
  BOARD_MEM_CELL board_mem_cell_5 (.EN(EN), .D(or_1_out[4]), .CLK(CLK), .RST(RESET), .Q(STATE[4]));
  BOARD_MEM_CELL board_mem_cell_6 (.EN(EN), .D(or_1_out[7]), .CLK(CLK), .RST(RESET), .Q(STATE[7]));
  BOARD_MEM_CELL board_mem_cell_7 (.EN(EN), .D(or_1_out[2]), .CLK(CLK), .RST(RESET), .Q(STATE[2]));
  BOARD_MEM_CELL board_mem_cell_8 (.EN(EN), .D(or_1_out[5]), .CLK(CLK), .RST(RESET), .Q(STATE[5]));
  BOARD_MEM_CELL board_mem_cell_9 (.EN(EN), .D(or_1_out[8]), .CLK(CLK), .RST(RESET), .Q(STATE[8]));
endmodule

module COL_DET (
  input  [8:0] STATE,
  input  [8:0] MOV,
  output OK
);

  wire nand_1_out, nand_2_out, nand_3_out, nand_4_out, nand_5_out, nand_6_out, nand_7_out, nand_8_out,
       nand_9_out;

  nand nand_1 (nand_1_out, STATE[0], MOV[0]);
  nand nand_2 (nand_2_out, STATE[3], MOV[3]);
  nand nand_3 (nand_3_out, STATE[6], MOV[6]);
  nand nand_4 (nand_4_out, STATE[1], MOV[1]);
  nand nand_5 (nand_5_out, STATE[4], MOV[4]);
  nand nand_6 (nand_6_out, STATE[7], MOV[7]);
  nand nand_7 (nand_7_out, STATE[2], MOV[2]);
  nand nand_8 (nand_8_out, STATE[5], MOV[5]);
  nand nand_9 (nand_9_out, STATE[8], MOV[8]);
  and and_1 (OK, nand_1_out, nand_4_out, nand_7_out, nand_2_out, nand_5_out, nand_8_out, nand_3_out, nand_6_out, nand_9_out);
endmodule

module P_MOV_OK (
  input  [8:0] B1_state,
  input  [8:0] B2_state,
  input  [8:0] pmov,
  output Player_Move_OK
);

  wire and_1_out, col_det_1_ok, col_det_2_ok, p_selection_ok_1_ok;

  COL_DET col_det_1 (.STATE(B1_state), .MOV(pmov), .OK(col_det_1_ok));
  COL_DET col_det_2 (.STATE(B2_state), .MOV(pmov), .OK(col_det_2_ok));
  P_SELECTION_OK p_selection_ok_1 (.INP(pmov), .OK(p_selection_ok_1_ok));
  and and_1 (and_1_out, col_det_1_ok, col_det_2_ok);
  and and_2 (Player_Move_OK, and_1_out, p_selection_ok_1_ok);

  // Notes on the sheet:
  //   HAS MOV SELECTED
  //   IS LEGAL
endmodule

module P2_SWITCH (
  input  [8:0] PLR_MOV,
  input  [8:0] CPU_MOV,
  input  doAI,
  output [8:0] OUT
);

  Multiplexer #(.width(9), .enable("false")) multiplexer_1 (.in0(PLR_MOV), .in1(CPU_MOV), .out(OUT), .sel(doAI));
endmodule

module WIN_DTCT (
  input  [8:0] STATE,
  output WIN
);

  wire nand_1_out, nand_2_out, nand_3_out, nand_4_out, nand_5_out, nand_6_out, nand_7_out, nand_8_out;

  nand nand_1 (nand_1_out, STATE[1], STATE[0], STATE[2]);
  nand nand_2 (nand_2_out, STATE[0], STATE[3], STATE[6]);
  nand nand_3 (nand_3_out, STATE[0], STATE[4], STATE[8]);
  nand nand_4 (nand_4_out, STATE[3], STATE[4], STATE[5]);
  nand nand_5 (nand_5_out, STATE[1], STATE[4], STATE[7]);
  nand nand_6 (nand_6_out, STATE[2], STATE[4], STATE[6]);
  nand nand_7 (nand_7_out, STATE[6], STATE[7], STATE[8]);
  nand nand_8 (nand_8_out, STATE[2], STATE[5], STATE[8]);
  nand nand_9 (WIN, nand_1_out, nand_4_out, nand_7_out, nand_2_out, nand_5_out, nand_8_out, nand_3_out, nand_6_out);

  // Other names for the same wires on the sheet: B0 = STATE[0]; B1 = STATE[1]; B2 = STATE[2]; B3 = STATE[3];
  //   B4 = STATE[4]; B5 = STATE[5]; B6 = STATE[6]; B7 = STATE[7]; B8 = STATE[8]
endmodule

module END_DTCT (
  input  [8:0] P1,
  input  [8:0] P2,
  output P1_WIN,
  output P2_WIN,
  output DRAW,
  output GAME_OVER
);

  wire draw_dtct_1_draw, not_1_out;

  WIN_DTCT win_dtct_1 (.STATE(P1), .WIN(P1_WIN));
  WIN_DTCT win_dtct_2 (.STATE(P2), .WIN(P2_WIN));
  DRAW_DTCT draw_dtct_1 (.P1(P1), .P2(P2), .DRAW(draw_dtct_1_draw));
  not not_1 (not_1_out, draw_dtct_1_draw);
  or or_1 (GAME_OVER, P1_WIN, P2_WIN, draw_dtct_1_draw);
  nor nor_1 (DRAW, P2_WIN, P1_WIN, not_1_out);
endmodule

module DRAW_DTCT (
  input  [8:0] P1,
  input  [8:0] P2,
  output DRAW
);

  wire [8:0] nor_1_out;

  assign nor_1_out = ~(P1 | P2);  // NOR_Gate nor_1, 9 bits wide
  nor nor_2 (DRAW, nor_1_out[0], nor_1_out[1], nor_1_out[2], nor_1_out[3], nor_1_out[4], nor_1_out[5], nor_1_out[6], nor_1_out[7], nor_1_out[8]);
endmodule

module STATE_MACHINE (
  input  CLK,
  input  Player_Move_OK,
  input  P2_is_CPU,
  input  P2_Starts,
  input  GameOver,
  input  RESET,
  output P1_Turn,
  output P2_Turn,
  output P1_Write_Enable,
  output P2_Write_Enable
);

  wire and_1_out, and_2_out, and_3_out, d_ff_1_q, not_1_out, not_2_out, not_3_out, not_4_out, or_1_out,
       xor_1_out;

  and and_1 (and_1_out, d_ff_1_q, P2_is_CPU);
  or or_1 (or_1_out, Player_Move_OK, and_1_out);
  xor xor_1 (xor_1_out, or_1_out, d_ff_1_q);
  D_Flip_Flop d_ff_1 (.clk(CLK), .D(xor_1_out), .Q(d_ff_1_q), .preset(and_2_out), .reset(and_3_out));  // open: Qn, en
  and and_2 (and_2_out, P2_Starts, RESET);
  and and_3 (and_3_out, not_1_out, RESET);
  not not_1 (not_1_out, P2_Starts);
  not not_2 (not_2_out, d_ff_1_q);
  not not_3 (not_3_out, GameOver);
  and and_4 (P1_Write_Enable, not_2_out, not_3_out, or_1_out);
  and and_5 (P2_Write_Enable, d_ff_1_q, not_3_out, or_1_out);
  not not_4 (not_4_out, d_ff_1_q);
  and and_6 (P1_Turn, not_4_out, not_3_out);
  and and_7 (P2_Turn, not_3_out, d_ff_1_q);
endmodule

module CPU (
  input  [8:0] P1,
  input  [8:0] P2,
  output [8:0] CPU
);

  wire cpu_block_cols_1_block_2, cpu_block_diags_1_block_2, cpu_block_rows_1_block_2,
       cpu_empty_corner_1_block_2, cpu_empty_side_1_block_2, cpu_forks_center_1_block_2,
       cpu_opposite_corners_1_block_2, cpu_win_cols_1_block_2, cpu_win_diags_1_block_2,
       cpu_win_rows_1_block_2, not_3_out;
  wire [7:0] rom_1_data;
  wire [8:0] cpu_block_cols_1_move, cpu_block_diags_1_move, cpu_block_rows_1_move, cpu_empty_corner_1_move,
       cpu_empty_side_1_move, cpu_forks_center_1_move, cpu_opposite_corners_1_move, cpu_win_cols_1_move,
       cpu_win_diags_1_move, cpu_win_rows_1_move, not_1_out, not_2_out, or_1_out, or_2_out, or_3_out,
       or_4_out, or_5_out, or_6_out, or_7_out, or_8_out, or_9_out, or_10_out;
  wire [8:8] nor_1_out;

  assign not_1_out = ~P1;  // NOT_Gate not_1, 9 bits wide
  assign not_2_out = ~P2;  // NOT_Gate not_2, 9 bits wide
  assign or_1_out = P1 | P2;  // OR_Gate or_1, 9 bits wide
  CPU_Win_Rows cpu_win_rows_1 (
    .nP1(not_1_out), .Block(1'b0), .nP2(not_2_out), .nEmpty(or_1_out), .Block_2(cpu_win_rows_1_block_2),
    .Move(cpu_win_rows_1_move));
  CPU_Block_Rows cpu_block_rows_1 (
    .nP1(not_1_out), .Block(cpu_win_diags_1_block_2), .nP2(not_2_out), .nEmpty(or_1_out),
    .Block_2(cpu_block_rows_1_block_2), .Move(cpu_block_rows_1_move));
  assign or_2_out = cpu_block_rows_1_move | or_7_out;  // OR_Gate or_2, 9 bits wide
  CPU_Forks_Center cpu_forks_center_1 (
    .nP1(not_1_out), .Block(cpu_block_diags_1_block_2), .nP2(not_2_out), .nEmpty(or_1_out),
    .Block_2(cpu_forks_center_1_block_2), .Move(cpu_forks_center_1_move));
  assign or_3_out = cpu_forks_center_1_move | or_8_out;  // OR_Gate or_3, 9 bits wide
  CPU_Win_Cols cpu_win_cols_1 (
    .nP1(not_1_out), .Block(cpu_win_rows_1_block_2), .nP2(not_2_out), .nEmpty(or_1_out),
    .Block_2(cpu_win_cols_1_block_2), .Move(cpu_win_cols_1_move));
  assign or_4_out = cpu_win_cols_1_move | cpu_win_rows_1_move;  // OR_Gate or_4, 9 bits wide
  CPU_Block_Cols cpu_block_cols_1 (
    .nP1(not_1_out), .Block(cpu_block_rows_1_block_2), .nP2(not_2_out), .nEmpty(or_1_out),
    .Block_2(cpu_block_cols_1_block_2), .Move(cpu_block_cols_1_move));
  assign or_5_out = cpu_block_cols_1_move | or_2_out;  // OR_Gate or_5, 9 bits wide
  CPU_Opposite_Corners cpu_opposite_corners_1 (
    .nP1(not_1_out), .nP2(not_2_out), .Block(cpu_forks_center_1_block_2), .nEmpty(or_1_out),
    .Block_2(cpu_opposite_corners_1_block_2), .Move(cpu_opposite_corners_1_move));
  assign or_6_out = cpu_opposite_corners_1_move | or_3_out;  // OR_Gate or_6, 9 bits wide
  CPU_Win_Diags cpu_win_diags_1 (
    .nP1(not_1_out), .Block(cpu_win_cols_1_block_2), .nP2(not_2_out), .nEmpty(or_1_out),
    .Block_2(cpu_win_diags_1_block_2), .Move(cpu_win_diags_1_move));
  CPU_Block_Diags cpu_block_diags_1 (
    .nP1(not_1_out), .Block(cpu_block_cols_1_block_2), .nP2(not_2_out), .nEmpty(or_1_out),
    .Block_2(cpu_block_diags_1_block_2), .Move(cpu_block_diags_1_move));
  CPU_Empty_Corner cpu_empty_corner_1 (
    .nP1(not_1_out), .nP2(not_2_out), .Block(cpu_opposite_corners_1_block_2), .nEmpty(or_1_out),
    .Block_2(cpu_empty_corner_1_block_2), .Move(cpu_empty_corner_1_move));
  ROM #(.addrWidth(18)) rom_1 (.addr({P2, P1}), .data(rom_1_data));  // open: sel
  assign or_7_out = cpu_win_diags_1_move | or_4_out;  // OR_Gate or_7, 9 bits wide
  assign or_8_out = cpu_block_diags_1_move | or_5_out;  // OR_Gate or_8, 9 bits wide
  assign or_9_out = cpu_empty_corner_1_move | or_6_out;  // OR_Gate or_9, 9 bits wide
  nor nor_1 (nor_1_out[8], rom_1_data[0], rom_1_data[1], rom_1_data[2], rom_1_data[3], rom_1_data[4], rom_1_data[5], rom_1_data[6], rom_1_data[7]);
  CPU_Empty_Side cpu_empty_side_1 (
    .nP1(not_1_out), .nP2(not_2_out), .Block(cpu_empty_corner_1_block_2), .nEmpty(or_1_out),
    .Block_2(cpu_empty_side_1_block_2), .Move(cpu_empty_side_1_move));
  not not_3 (not_3_out, cpu_empty_side_1_block_2);
  assign or_10_out = cpu_empty_side_1_move | or_9_out;  // OR_Gate or_10, 9 bits wide
  LED No_move_found (.in(not_3_out));
  Multiplexer #(.width(9), .enable("false")) multiplexer_1 (
    .in0(or_10_out), .in1({nor_1_out[8], rom_1_data}), .out(CPU), .sel(1'b1));
  LED led_1 (.in(CPU[0]));
  LED led_2 (.in(CPU[3]));
  LED led_3 (.in(CPU[6]));
  LED led_4 (.in(CPU[1]));
  LED led_5 (.in(CPU[4]));
  LED led_6 (.in(CPU[7]));
  LED led_7 (.in(CPU[2]));
  LED led_8 (.in(CPU[5]));
  LED led_9 (.in(CPU[8]));

  // Notes on the sheet:
  //   Forks/Center
  //   Win - Row
  //   Block - Row
  //   Win - Col
  //   Block - Col
  //   Opposite Corner
  //   Win - Diag
  //   Block - Diag
  //   Empty Corner
  //   contents of rom_1 (hex, n*v repeats v):
  //   10 10 10 4 10 2 1 ff 10 40 10 4 10 2 1 ff 40 0 80 4 40 2 1 ff 20 20 20 4 20 2 1 ff 10 10 10 4 0 2 1
  //   ff 10 10 10 4 10 2 1 ff 8 8 8 4 8 2 1 9*ff 10 8 10 4 10 2 1 ff 1 ff 1 ff 1 ff 1 ff 4 8 80 4 4*ff 20
  //   ff 20 5*ff 10 8 10 4 0 2 1 ff 10 ff 10 ff 10 ff 1 ff 8 8 8 4 12*ff 10 10 10 4 10 2 1 ff 10 40 10 4
  //   10 2 1 ff 2 2 ff ff 2 2 ff ff 20 20 ff ff 20 2 ff ff 10 10 10 4 0 2 1 ff 10 10 10 4 10 2 1 ff 8 8 ff
  //   ff 8 2 10*ff 0 0 0 4 0 2 1 ff 0 ff 0 ff 0 ff 1 ff 0 0 6*ff 20 7*ff 0 0 0 4 0 2 1 ff 10 ff 10 ff 10
  //   ff ff ff 8 8 14*ff 10 10 10 4 20 2 1 ff 10 40 10 4 20 2 1 ff 1 ff 80 ff 20 ff 1 ff 20 ff 20 ff 20 ff
  //   1 ff 4*4 4*ff 10 10 10 4 4*ff 8 ff 8 13*ff 80 80 80 4 80 2 1 ff 80 ff 80 ff 80 ff 1 ff 80 ff 80 5*ff
  //   20 ff 20 5*ff 80 80 80 4 4*ff 10 ff 10 5*ff 8 ff 8 13*ff 40 40 40 4 40 2 1 ff 40 40 40 4 40 2 1 ff
  //   40 ff ff ff 40 ff ff ff 20 ff ff ff 20 ff ff ff 40 40 40 4 4*ff 10 10 10 5*ff 8 79*ff 10 ff 10 ff 10
  //   ff 10 ff 10 ff 10 ff 10 ff 10 ff 4 ff 80 ff 40 ff 80 ff 20 ff 20 ff 20 ff 20 ff 10 ff 10 ff 0 ff 0
  //   ff 10 ff 10 ff 10 ff 10 ff 8 ff 8 ff 8 ff 8 9*ff 10 ff 10 ff 10 ff 10 ff 10 ff 10 ff 10 ff 10 ff 4
  //   ff 80 5*ff 20 ff 20 5*ff 10 ff 10 ff 0 ff 0 ff 10 ff 10 ff 10 ff 10 ff 8 ff 8 13*ff 10 ff 10 ff 10
  //   ff 10 ff 10 ff 10 ff 10 ff 10 ff 2 ff ff ff 2 ff ff ff 20 ff ff ff 20 ff ff ff 10 ff 10 ff 0 ff 10
  //   ff 10 ff 10 ff 10 ff 10 ff 8 ff ff ff 8 11*ff 0 ff 0 ff 0 ff 0 ff 0 ff 0 ff 0 ff 0 ff 0 7*ff 20 7*ff
  //   0 ff 0 ff 0 ff 0 ff 10 ff 10 ff 10 ff 10 ff 8 15*ff 10 ff 10 ff 20 ff 20 ff 10 ff 10 ff 20 ff 20 ff
  //   40 ff 80 ff 20 ff 80 ff 20 ff 20 ff 20 ff 20 ff 4 ff 4 5*ff 10 ff 10 5*ff 8 ff 8 13*ff 80 ff 80 ff
  //   80 ff 80 ff 80 ff 80 ff 80 ff 80 ff 80 ff 80 5*ff 20 ff 20 5*ff 80 ff 80 5*ff 10 ff 10 5*ff 8 ff 8
  //   13*ff 40 ff 40 ff 40 ff 40 ff 40 ff 40 ff 40 ff 40 ff 40 ff ff ff 40 ff ff ff 20 ff ff ff 20 ff ff
  //   ff 40 ff 40 5*ff 10 ff 10 5*ff 8 79*ff 10 10 ff ff 10 10 ff ff 10 40 ff ff 10 40 ff ff 0 0 ff ff 40
  //   0 ff ff 20 20 ff ff 20 20 ff ff 10 10 ff ff 0 0 ff ff 10 10 ff ff 10 10 ff ff 8 8 ff ff 8 8 10*ff 10
  //   8 ff ff 10 8 ff ff 1 ff ff ff 1 ff ff ff 4 8 6*ff 20 7*ff 10 8 ff ff 0 8 ff ff 10 ff ff ff 10 ff ff
  //   ff 8 8 14*ff 10 10 ff ff 10 10 ff ff 10 40 ff ff 10 40 ff ff 1 0 ff ff 40 0 ff ff 20 20 ff ff 20 20
  //   ff ff 10 10 ff ff 0 0 ff ff 10 10 ff ff 10 10 ff ff 8 8 ff ff 8 8 10*ff 0 0 ff ff 0 0 ff ff 0 ff ff
  //   ff 0 ff ff ff 0 0 6*ff 20 7*ff 0 0 ff ff 0 0 ff ff 10 ff ff ff 10 ff ff ff 8 8 14*ff 10 10 ff ff 20
  //   20 ff ff 10 40 ff ff 20 40 ff ff 1 ff ff ff 20 ff ff ff 20 ff ff ff 20 ff ff ff 4 4 6*ff 10 10 6*ff
  //   8 15*ff 80 80 ff ff 80 80 ff ff 80 ff ff ff 80 ff ff ff 80 7*ff 20 7*ff 80 80 6*ff 10 7*ff 8 15*ff
  //   40 40 ff ff 40 40 ff ff 40 40 ff ff 40 40 ff ff 40 ff ff ff 40 ff ff ff 20 ff ff ff 20 ff ff ff 40
  //   40 6*ff 10 10 6*ff 8 79*ff 4 ff ff ff 10 ff ff ff 4 ff ff ff 10 ff ff ff 4 ff ff ff 40 ff ff ff 4 ff
  //   ff ff 20 ff ff ff 4 ff ff ff 0 ff ff ff 4 ff ff ff 10 ff ff ff 4 ff ff ff 8 11*ff 4 ff ff ff 10 ff
  //   ff ff 4 ff ff ff 10 ff ff ff 4 7*ff 4 7*ff 4 ff ff ff 0 ff ff ff 4 ff ff ff 10 ff ff ff 4 15*ff 4 ff
  //   ff ff 10 ff ff ff 4 ff ff ff 10 ff ff ff 4 ff ff ff 40 ff ff ff 4 ff ff ff 20 ff ff ff 4 ff ff ff 0
  //   ff ff ff 4 ff ff ff 10 ff ff ff 4 ff ff ff 8 11*ff 4 ff ff ff 0 ff ff ff 4 ff ff ff 0 ff ff ff 4
  //   7*ff 4 7*ff 4 ff ff ff 0 ff ff ff 4 ff ff ff 10 ff ff ff 4 15*ff 4 ff ff ff 20 ff ff ff 4 ff ff ff
  //   20 ff ff ff 4 ff ff ff 20 ff ff ff 4 ff ff ff 20 ff ff ff 4 7*ff 4 7*ff 4 15*ff 4 ff ff ff 80 ff ff
  //   ff 4 ff ff ff 80 ff ff ff 4 7*ff 4 7*ff 4 7*ff 4 7*ff 4 15*ff 4 ff ff ff 40 ff ff ff 4 ff ff ff 40
  //   ff ff ff 4 ff ff ff 40 ff ff ff 4 ff ff ff 20 ff ff ff 4 7*ff 4 7*ff 4 79*ff 4*10 4*ff 10 40 10 40
  //   4*ff 1 0 80 80 4*ff 4*20 4*ff 4*10 4*ff 4*10 4*ff 4*8 12*ff 10 8 10 8 4*ff 1 ff 1 5*ff 0 8 80 8 4*ff
  //   20 ff 20 5*ff 10 8 10 8 4*ff 10 ff 10 5*ff 4*8 12*ff 4*10 4*ff 10 40 10 40 4*ff 2 2 6*ff 20 20 6*ff
  //   4*10 4*ff 4*10 4*ff 8 8 14*ff 4*0 4*ff 0 ff 0 5*ff 0 0 6*ff 20 7*ff 4*0 4*ff 10 ff 10 5*ff 8 8 14*ff
  //   4*10 4*ff 10 40 10 40 4*ff 1 ff 80 5*ff 20 ff 20 5*ff 4*10 4*ff 4*10 4*ff 8 ff 8 13*ff 4*80 4*ff 80
  //   ff 80 5*f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
  //   Empty Side
  //   0 = Engine
  //   1 = ROM
endmodule

module P_SELECTION_OK (
  input  [8:0] INP,
  output OK
);

  wire and_1_out, nand_1_out, nand_2_out, nand_3_out, nand_4_out, nand_5_out, nand_6_out, nand_7_out,
       nand_8_out, or_1_out, or_2_out, or_3_out, or_4_out, or_5_out, or_6_out, or_7_out, or_8_out;

  or or_1 (or_1_out, INP[1], INP[0]);
  or or_2 (or_2_out, INP[2], or_1_out);
  or or_3 (or_3_out, INP[3], or_2_out);
  or or_4 (or_4_out, INP[4], or_3_out);
  or or_5 (or_5_out, INP[5], or_4_out);
  or or_6 (or_6_out, INP[6], or_5_out);
  or or_7 (or_7_out, INP[7], or_6_out);
  or or_8 (or_8_out, INP[8], or_7_out);
  nand nand_1 (nand_1_out, INP[0], INP[1]);
  nand nand_2 (nand_2_out, or_1_out, INP[2]);
  nand nand_3 (nand_3_out, or_2_out, INP[3]);
  nand nand_4 (nand_4_out, or_3_out, INP[4]);
  nand nand_5 (nand_5_out, or_4_out, INP[5]);
  nand nand_6 (nand_6_out, or_5_out, INP[6]);
  nand nand_7 (nand_7_out, or_6_out, INP[7]);
  nand nand_8 (nand_8_out, or_7_out, INP[8]);
  and and_1 (and_1_out, nand_1_out, nand_2_out, nand_3_out, nand_4_out, nand_5_out, nand_6_out, nand_7_out, nand_8_out);
  and and_2 (OK, and_1_out, or_8_out);
endmodule

module BOARD_MEM_CELL (
  input  EN,
  input  D,
  input  CLK,
  input  RST,
  output Q
);

  wire d_ff_1_qn, nand_1_out, nand_2_out;

  nand nand_1 (nand_1_out, EN, D);
  nand nand_2 (nand_2_out, nand_1_out, d_ff_1_qn);
  D_Flip_Flop d_ff_1 (.clk(CLK), .D(nand_2_out), .Q(Q), .Qn(d_ff_1_qn), .reset(RST));  // open: preset, en
endmodule

module CPU_Win_Rows (
  input  [8:0] nP1,
  input  Block,
  input  [8:0] nP2,
  input  [8:0] nEmpty,
  output Block_2,
  output [8:0] Move
);

  wire or_1_out, or_3_out, or_5_out, or_10_out, or_11_out, or_12_out, or_16_out, or_17_out;
  wire [8:0] nor_1_out, or_2_out, or_4_out, or_6_out, or_7_out, or_8_out, or_9_out, or_13_out, or_14_out,
       pull_resistor_2_node, pull_resistor_3_node, pull_resistor_4_node, pull_resistor_5_node,
       pull_resistor_6_node, pull_resistor_7_node, pull_resistor_8_node, pull_resistor_9_node;

  nor nor_1 (nor_1_out[0], nP2[1], nP2[2], nEmpty[0], Block);
  Pull_Resistor pull_resistor_1 (.node(nor_1_out));
  nor nor_2 (pull_resistor_2_node[3], nP2[4], nP2[5], nEmpty[3], or_16_out);
  Pull_Resistor pull_resistor_2 (.node(pull_resistor_2_node));
  nor nor_3 (pull_resistor_3_node[6], nP2[7], nP2[8], nEmpty[6], or_17_out);
  Pull_Resistor pull_resistor_3 (.node(pull_resistor_3_node));
  or or_1 (or_1_out, nor_1_out[0], Block);
  assign or_2_out = nor_1_out | {9{1'b0}};  // OR_Gate or_2, 9 bits wide
  or or_3 (or_3_out, pull_resistor_2_node[3], or_16_out);
  assign or_4_out = pull_resistor_2_node | or_13_out;  // OR_Gate or_4, 9 bits wide
  or or_5 (or_5_out, pull_resistor_3_node[6], or_17_out);
  assign or_6_out = pull_resistor_3_node | or_14_out;  // OR_Gate or_6, 9 bits wide
  Pull_Resistor pull_resistor_4 (.node(pull_resistor_4_node));
  Pull_Resistor pull_resistor_5 (.node(pull_resistor_5_node));
  Pull_Resistor pull_resistor_6 (.node(pull_resistor_6_node));
  nor nor_4 (pull_resistor_4_node[1], nP2[0], nP2[2], nEmpty[1], or_1_out);
  assign or_7_out = pull_resistor_4_node | or_2_out;  // OR_Gate or_7, 9 bits wide
  nor nor_5 (pull_resistor_5_node[4], nP2[3], nP2[5], nEmpty[4], or_3_out);
  assign or_8_out = pull_resistor_5_node | or_4_out;  // OR_Gate or_8, 9 bits wide
  nor nor_6 (pull_resistor_6_node[7], nP2[6], nP2[8], nEmpty[7], or_5_out);
  assign or_9_out = pull_resistor_6_node | or_6_out;  // OR_Gate or_9, 9 bits wide
  or or_10 (or_10_out, pull_resistor_4_node[1], or_1_out);
  or or_11 (or_11_out, pull_resistor_5_node[4], or_3_out);
  or or_12 (or_12_out, pull_resistor_6_node[7], or_5_out);
  nor nor_7 (pull_resistor_7_node[2], nP2[0], nP2[1], nEmpty[2], or_10_out);
  Pull_Resistor pull_resistor_7 (.node(pull_resistor_7_node));
  assign or_13_out = pull_resistor_7_node | or_7_out;  // OR_Gate or_13, 9 bits wide
  nor nor_8 (pull_resistor_8_node[5], nP2[3], nP2[4], nEmpty[5], or_11_out);
  Pull_Resistor pull_resistor_8 (.node(pull_resistor_8_node));
  assign or_14_out = pull_resistor_8_node | or_8_out;  // OR_Gate or_14, 9 bits wide
  nor nor_9 (pull_resistor_9_node[8], nP2[6], nP2[7], nEmpty[8], or_12_out);
  Pull_Resistor pull_resistor_9 (.node(pull_resistor_9_node));
  assign Move = pull_resistor_9_node | or_9_out;  // OR_Gate or_15, 9 bits wide
  or or_16 (or_16_out, pull_resistor_7_node[2], or_10_out);
  or or_17 (or_17_out, pull_resistor_8_node[5], or_11_out);
  or or_18 (Block_2, pull_resistor_9_node[8], or_12_out);

  // Other names for the same wires on the sheet: E0 = nEmpty[0]; E1 = nEmpty[1]; E2 = nEmpty[2]; E3 = nEmpty[3];
  //   E4 = nEmpty[4]; E5 = nEmpty[5]; E6 = nEmpty[6]; E7 = nEmpty[7]; E8 = nEmpty[8]; A0 = nP1[0]; A1 = nP1[1];
  //   A2 = nP1[2]; A3 = nP1[3]; A4 = nP1[4]; A5 = nP1[5]; A6 = nP1[6]; A7 = nP1[7]; A8 = nP1[8]; B0 = nP2[0];
  //   B1 = nP2[1]; B2 = nP2[2]; B3 = nP2[3]; B4 = nP2[4]; B5 = nP2[5]; B6 = nP2[6]; B7 = nP2[7]; B8 = nP2[8]
endmodule

module CPU_Win_Cols (
  input  [8:0] nP1,
  input  Block,
  input  [8:0] nP2,
  input  [8:0] nEmpty,
  output Block_2,
  output [8:0] Move
);

  wire or_1_out, or_3_out, or_5_out, or_10_out, or_11_out, or_12_out, or_16_out, or_17_out;
  wire [8:0] nor_1_out, or_2_out, or_4_out, or_6_out, or_7_out, or_8_out, or_9_out, or_13_out, or_14_out,
       pull_resistor_2_node, pull_resistor_3_node, pull_resistor_4_node, pull_resistor_5_node,
       pull_resistor_6_node, pull_resistor_7_node, pull_resistor_8_node, pull_resistor_9_node;

  nor nor_1 (nor_1_out[0], nP2[3], nP2[6], nEmpty[0], Block);
  Pull_Resistor pull_resistor_1 (.node(nor_1_out));
  nor nor_2 (pull_resistor_2_node[1], nP2[4], nP2[7], nEmpty[1], or_16_out);
  Pull_Resistor pull_resistor_2 (.node(pull_resistor_2_node));
  nor nor_3 (pull_resistor_3_node[2], nP2[5], nP2[8], nEmpty[2], or_17_out);
  Pull_Resistor pull_resistor_3 (.node(pull_resistor_3_node));
  or or_1 (or_1_out, nor_1_out[0], Block);
  assign or_2_out = nor_1_out | {9{1'b0}};  // OR_Gate or_2, 9 bits wide
  or or_3 (or_3_out, pull_resistor_2_node[1], or_16_out);
  assign or_4_out = pull_resistor_2_node | or_13_out;  // OR_Gate or_4, 9 bits wide
  or or_5 (or_5_out, pull_resistor_3_node[2], or_17_out);
  assign or_6_out = pull_resistor_3_node | or_14_out;  // OR_Gate or_6, 9 bits wide
  Pull_Resistor pull_resistor_4 (.node(pull_resistor_4_node));
  Pull_Resistor pull_resistor_5 (.node(pull_resistor_5_node));
  Pull_Resistor pull_resistor_6 (.node(pull_resistor_6_node));
  nor nor_4 (pull_resistor_4_node[3], nP2[0], nP2[6], nEmpty[3], or_1_out);
  assign or_7_out = pull_resistor_4_node | or_2_out;  // OR_Gate or_7, 9 bits wide
  nor nor_5 (pull_resistor_5_node[4], nP2[1], nP2[7], nEmpty[4], or_3_out);
  assign or_8_out = pull_resistor_5_node | or_4_out;  // OR_Gate or_8, 9 bits wide
  nor nor_6 (pull_resistor_6_node[5], nP2[2], nP2[8], nEmpty[5], or_5_out);
  assign or_9_out = pull_resistor_6_node | or_6_out;  // OR_Gate or_9, 9 bits wide
  or or_10 (or_10_out, pull_resistor_4_node[3], or_1_out);
  or or_11 (or_11_out, pull_resistor_5_node[4], or_3_out);
  or or_12 (or_12_out, pull_resistor_6_node[5], or_5_out);
  nor nor_7 (pull_resistor_7_node[6], nP2[0], nP2[3], nEmpty[6], or_10_out);
  Pull_Resistor pull_resistor_7 (.node(pull_resistor_7_node));
  assign or_13_out = pull_resistor_7_node | or_7_out;  // OR_Gate or_13, 9 bits wide
  nor nor_8 (pull_resistor_8_node[7], nP2[1], nP2[4], nEmpty[7], or_11_out);
  Pull_Resistor pull_resistor_8 (.node(pull_resistor_8_node));
  assign or_14_out = pull_resistor_8_node | or_8_out;  // OR_Gate or_14, 9 bits wide
  nor nor_9 (pull_resistor_9_node[8], nP2[2], nP2[5], nEmpty[8], or_12_out);
  Pull_Resistor pull_resistor_9 (.node(pull_resistor_9_node));
  assign Move = pull_resistor_9_node | or_9_out;  // OR_Gate or_15, 9 bits wide
  or or_16 (or_16_out, pull_resistor_7_node[6], or_10_out);
  or or_17 (or_17_out, pull_resistor_8_node[7], or_11_out);
  or or_18 (Block_2, pull_resistor_9_node[8], or_12_out);

  // Other names for the same wires on the sheet: E0 = nEmpty[0]; E1 = nEmpty[1]; E2 = nEmpty[2]; E3 = nEmpty[3];
  //   E4 = nEmpty[4]; E5 = nEmpty[5]; E6 = nEmpty[6]; E7 = nEmpty[7]; E8 = nEmpty[8]; A0 = nP1[0]; A1 = nP1[1];
  //   A2 = nP1[2]; A3 = nP1[3]; A4 = nP1[4]; A5 = nP1[5]; A6 = nP1[6]; A7 = nP1[7]; A8 = nP1[8]; B0 = nP2[0];
  //   B1 = nP2[1]; B2 = nP2[2]; B3 = nP2[3]; B4 = nP2[4]; B5 = nP2[5]; B6 = nP2[6]; B7 = nP2[7]; B8 = nP2[8]
endmodule

module CPU_Win_Diags (
  input  [8:0] nP1,
  input  Block,
  input  [8:0] nP2,
  input  [8:0] nEmpty,
  output Block_2,
  output [8:0] Move
);

  wire or_1_out, or_3_out, or_7_out, or_8_out, or_11_out;
  wire [8:0] nor_1_out, or_2_out, or_4_out, or_5_out, or_6_out, or_9_out, pull_resistor_2_node,
       pull_resistor_3_node, pull_resistor_4_node, pull_resistor_5_node, pull_resistor_6_node;

  nor nor_1 (nor_1_out[0], nP2[4], nP2[8], nEmpty[0], Block);
  Pull_Resistor pull_resistor_1 (.node(nor_1_out));
  nor nor_2 (pull_resistor_2_node[2], nP2[4], nP2[6], nEmpty[2], or_11_out);
  Pull_Resistor pull_resistor_2 (.node(pull_resistor_2_node));
  or or_1 (or_1_out, nor_1_out[0], Block);
  assign or_2_out = nor_1_out | {9{1'b0}};  // OR_Gate or_2, 9 bits wide
  or or_3 (or_3_out, pull_resistor_2_node[2], or_11_out);
  assign or_4_out = pull_resistor_2_node | or_9_out;  // OR_Gate or_4, 9 bits wide
  Pull_Resistor pull_resistor_3 (.node(pull_resistor_3_node));
  Pull_Resistor pull_resistor_4 (.node(pull_resistor_4_node));
  nor nor_3 (pull_resistor_3_node[4], nP2[0], nP2[8], nEmpty[4], or_1_out);
  assign or_5_out = pull_resistor_3_node | or_2_out;  // OR_Gate or_5, 9 bits wide
  nor nor_4 (pull_resistor_4_node[4], nP2[2], nP2[6], nEmpty[4], or_3_out);
  assign or_6_out = pull_resistor_4_node | or_4_out;  // OR_Gate or_6, 9 bits wide
  or or_7 (or_7_out, pull_resistor_3_node[4], or_1_out);
  or or_8 (or_8_out, pull_resistor_4_node[4], or_3_out);
  nor nor_5 (pull_resistor_5_node[8], nP2[0], nP2[4], nEmpty[8], or_7_out);
  Pull_Resistor pull_resistor_5 (.node(pull_resistor_5_node));
  assign or_9_out = pull_resistor_5_node | or_5_out;  // OR_Gate or_9, 9 bits wide
  nor nor_6 (pull_resistor_6_node[6], nP2[2], nP2[4], nEmpty[6], or_8_out);
  Pull_Resistor pull_resistor_6 (.node(pull_resistor_6_node));
  assign Move = pull_resistor_6_node | or_6_out;  // OR_Gate or_10, 9 bits wide
  or or_11 (or_11_out, pull_resistor_5_node[8], or_7_out);
  or or_12 (Block_2, pull_resistor_6_node[6], or_8_out);

  // Other names for the same wires on the sheet: E0 = nEmpty[0]; E1 = nEmpty[1]; E2 = nEmpty[2]; E3 = nEmpty[3];
  //   E4 = nEmpty[4]; E5 = nEmpty[5]; E6 = nEmpty[6]; E7 = nEmpty[7]; E8 = nEmpty[8]; A0 = nP1[0]; A1 = nP1[1];
  //   A2 = nP1[2]; A3 = nP1[3]; A4 = nP1[4]; A5 = nP1[5]; A6 = nP1[6]; A7 = nP1[7]; A8 = nP1[8]; B0 = nP2[0];
  //   B1 = nP2[1]; B2 = nP2[2]; B3 = nP2[3]; B4 = nP2[4]; B5 = nP2[5]; B6 = nP2[6]; B7 = nP2[7]; B8 = nP2[8]
endmodule

module CPU_Block_Rows (
  input  [8:0] nP1,
  input  Block,
  input  [8:0] nP2,
  input  [8:0] nEmpty,
  output Block_2,
  output [8:0] Move
);

  wire or_1_out, or_3_out, or_5_out, or_10_out, or_11_out, or_12_out, or_16_out, or_17_out;
  wire [8:0] nor_1_out, or_2_out, or_4_out, or_6_out, or_7_out, or_8_out, or_9_out, or_13_out, or_14_out,
       pull_resistor_2_node, pull_resistor_3_node, pull_resistor_4_node, pull_resistor_5_node,
       pull_resistor_6_node, pull_resistor_7_node, pull_resistor_8_node, pull_resistor_9_node;

  nor nor_1 (nor_1_out[0], nP1[2], nP1[1], nEmpty[0], Block);
  Pull_Resistor pull_resistor_1 (.node(nor_1_out));
  nor nor_2 (pull_resistor_2_node[3], nP1[4], nP1[5], nEmpty[3], or_16_out);
  Pull_Resistor pull_resistor_2 (.node(pull_resistor_2_node));
  nor nor_3 (pull_resistor_3_node[6], nP1[7], nP1[8], nEmpty[6], or_17_out);
  Pull_Resistor pull_resistor_3 (.node(pull_resistor_3_node));
  or or_1 (or_1_out, nor_1_out[0], Block);
  assign or_2_out = nor_1_out | {9{1'b0}};  // OR_Gate or_2, 9 bits wide
  or or_3 (or_3_out, pull_resistor_2_node[3], or_16_out);
  assign or_4_out = pull_resistor_2_node | or_13_out;  // OR_Gate or_4, 9 bits wide
  or or_5 (or_5_out, pull_resistor_3_node[6], or_17_out);
  assign or_6_out = pull_resistor_3_node | or_14_out;  // OR_Gate or_6, 9 bits wide
  Pull_Resistor pull_resistor_4 (.node(pull_resistor_4_node));
  Pull_Resistor pull_resistor_5 (.node(pull_resistor_5_node));
  Pull_Resistor pull_resistor_6 (.node(pull_resistor_6_node));
  nor nor_4 (pull_resistor_4_node[1], nP1[2], nP1[0], nEmpty[1], or_1_out);
  assign or_7_out = pull_resistor_4_node | or_2_out;  // OR_Gate or_7, 9 bits wide
  nor nor_5 (pull_resistor_5_node[4], nP1[3], nP1[5], nEmpty[4], or_3_out);
  assign or_8_out = pull_resistor_5_node | or_4_out;  // OR_Gate or_8, 9 bits wide
  nor nor_6 (pull_resistor_6_node[7], nP1[8], nP1[6], nEmpty[7], or_5_out);
  assign or_9_out = pull_resistor_6_node | or_6_out;  // OR_Gate or_9, 9 bits wide
  or or_10 (or_10_out, pull_resistor_4_node[1], or_1_out);
  or or_11 (or_11_out, pull_resistor_5_node[4], or_3_out);
  or or_12 (or_12_out, pull_resistor_6_node[7], or_5_out);
  nor nor_7 (pull_resistor_7_node[2], nP1[1], nP1[0], nEmpty[2], or_10_out);
  Pull_Resistor pull_resistor_7 (.node(pull_resistor_7_node));
  assign or_13_out = pull_resistor_7_node | or_7_out;  // OR_Gate or_13, 9 bits wide
  nor nor_8 (pull_resistor_8_node[5], nP1[3], nP1[5], nEmpty[5], or_11_out);
  Pull_Resistor pull_resistor_8 (.node(pull_resistor_8_node));
  assign or_14_out = pull_resistor_8_node | or_8_out;  // OR_Gate or_14, 9 bits wide
  nor nor_9 (pull_resistor_9_node[8], nP1[7], nP1[6], nEmpty[8], or_12_out);
  Pull_Resistor pull_resistor_9 (.node(pull_resistor_9_node));
  assign Move = pull_resistor_9_node | or_9_out;  // OR_Gate or_15, 9 bits wide
  or or_16 (or_16_out, pull_resistor_7_node[2], or_10_out);
  or or_17 (or_17_out, pull_resistor_8_node[5], or_11_out);
  or or_18 (Block_2, pull_resistor_9_node[8], or_12_out);

  // Other names for the same wires on the sheet: E0 = nEmpty[0]; E1 = nEmpty[1]; E2 = nEmpty[2]; E3 = nEmpty[3];
  //   E4 = nEmpty[4]; E5 = nEmpty[5]; E6 = nEmpty[6]; E7 = nEmpty[7]; E8 = nEmpty[8]; A0 = nP1[0]; A1 = nP1[1];
  //   A2 = nP1[2]; A3 = nP1[3]; A4 = nP1[4]; A5 = nP1[5]; A6 = nP1[6]; A7 = nP1[7]; A8 = nP1[8]; B0 = nP2[0];
  //   B1 = nP2[1]; B2 = nP2[2]; B3 = nP2[3]; B4 = nP2[4]; B5 = nP2[5]; B6 = nP2[6]; B7 = nP2[7]; B8 = nP2[8]
endmodule

module CPU_Block_Cols (
  input  [8:0] nP1,
  input  Block,
  input  [8:0] nP2,
  input  [8:0] nEmpty,
  output Block_2,
  output [8:0] Move
);

  wire or_1_out, or_3_out, or_5_out, or_10_out, or_11_out, or_12_out, or_16_out, or_17_out;
  wire [8:0] nor_1_out, or_2_out, or_4_out, or_6_out, or_7_out, or_8_out, or_9_out, or_13_out, or_14_out,
       pull_resistor_2_node, pull_resistor_3_node, pull_resistor_4_node, pull_resistor_5_node,
       pull_resistor_6_node, pull_resistor_7_node, pull_resistor_8_node, pull_resistor_9_node;

  nor nor_1 (nor_1_out[0], nP1[3], nP1[6], nEmpty[0], Block);
  Pull_Resistor pull_resistor_1 (.node(nor_1_out));
  nor nor_2 (pull_resistor_2_node[1], nP1[4], nP1[7], nEmpty[1], or_16_out);
  Pull_Resistor pull_resistor_2 (.node(pull_resistor_2_node));
  nor nor_3 (pull_resistor_3_node[2], nP1[5], nP1[8], nEmpty[2], or_17_out);
  Pull_Resistor pull_resistor_3 (.node(pull_resistor_3_node));
  or or_1 (or_1_out, nor_1_out[0], Block);
  assign or_2_out = nor_1_out | {9{1'b0}};  // OR_Gate or_2, 9 bits wide
  or or_3 (or_3_out, pull_resistor_2_node[1], or_16_out);
  assign or_4_out = pull_resistor_2_node | or_13_out;  // OR_Gate or_4, 9 bits wide
  or or_5 (or_5_out, pull_resistor_3_node[2], or_17_out);
  assign or_6_out = pull_resistor_3_node | or_14_out;  // OR_Gate or_6, 9 bits wide
  Pull_Resistor pull_resistor_4 (.node(pull_resistor_4_node));
  Pull_Resistor pull_resistor_5 (.node(pull_resistor_5_node));
  Pull_Resistor pull_resistor_6 (.node(pull_resistor_6_node));
  nor nor_4 (pull_resistor_4_node[3], nP1[0], nP1[6], nEmpty[3], or_1_out);
  assign or_7_out = pull_resistor_4_node | or_2_out;  // OR_Gate or_7, 9 bits wide
  nor nor_5 (pull_resistor_5_node[4], nP1[1], nP1[7], nEmpty[4], or_3_out);
  assign or_8_out = pull_resistor_5_node | or_4_out;  // OR_Gate or_8, 9 bits wide
  nor nor_6 (pull_resistor_6_node[5], nP1[2], nP1[8], nEmpty[5], or_5_out);
  assign or_9_out = pull_resistor_6_node | or_6_out;  // OR_Gate or_9, 9 bits wide
  or or_10 (or_10_out, pull_resistor_4_node[3], or_1_out);
  or or_11 (or_11_out, pull_resistor_5_node[4], or_3_out);
  or or_12 (or_12_out, pull_resistor_6_node[5], or_5_out);
  nor nor_7 (pull_resistor_7_node[6], nP1[0], nP1[3], nEmpty[6], or_10_out);
  Pull_Resistor pull_resistor_7 (.node(pull_resistor_7_node));
  assign or_13_out = pull_resistor_7_node | or_7_out;  // OR_Gate or_13, 9 bits wide
  nor nor_8 (pull_resistor_8_node[7], nP1[1], nP1[4], nEmpty[7], or_11_out);
  Pull_Resistor pull_resistor_8 (.node(pull_resistor_8_node));
  assign or_14_out = pull_resistor_8_node | or_8_out;  // OR_Gate or_14, 9 bits wide
  nor nor_9 (pull_resistor_9_node[8], nP1[2], nP1[5], nEmpty[8], or_12_out);
  Pull_Resistor pull_resistor_9 (.node(pull_resistor_9_node));
  assign Move = pull_resistor_9_node | or_9_out;  // OR_Gate or_15, 9 bits wide
  or or_16 (or_16_out, pull_resistor_7_node[6], or_10_out);
  or or_17 (or_17_out, pull_resistor_8_node[7], or_11_out);
  or or_18 (Block_2, pull_resistor_9_node[8], or_12_out);

  // Other names for the same wires on the sheet: E0 = nEmpty[0]; E1 = nEmpty[1]; E2 = nEmpty[2]; E3 = nEmpty[3];
  //   E4 = nEmpty[4]; E5 = nEmpty[5]; E6 = nEmpty[6]; E7 = nEmpty[7]; E8 = nEmpty[8]; A0 = nP1[0]; A1 = nP1[1];
  //   A2 = nP1[2]; A3 = nP1[3]; A4 = nP1[4]; A5 = nP1[5]; A6 = nP1[6]; A7 = nP1[7]; A8 = nP1[8]; B0 = nP2[0];
  //   B1 = nP2[1]; B2 = nP2[2]; B3 = nP2[3]; B4 = nP2[4]; B5 = nP2[5]; B6 = nP2[6]; B7 = nP2[7]; B8 = nP2[8]
endmodule

module CPU_Block_Diags (
  input  [8:0] nP1,
  input  Block,
  input  [8:0] nP2,
  input  [8:0] nEmpty,
  output Block_2,
  output [8:0] Move
);

  wire or_1_out, or_3_out, or_7_out, or_8_out, or_11_out;
  wire [8:0] nor_1_out, or_2_out, or_4_out, or_5_out, or_6_out, or_9_out, pull_resistor_2_node,
       pull_resistor_3_node, pull_resistor_4_node, pull_resistor_5_node, pull_resistor_6_node;

  nor nor_1 (nor_1_out[0], nP1[4], nP1[6], nEmpty[0], Block);
  Pull_Resistor pull_resistor_1 (.node(nor_1_out));
  nor nor_2 (pull_resistor_2_node[2], nP1[4], nP1[8], nEmpty[2], or_11_out);
  Pull_Resistor pull_resistor_2 (.node(pull_resistor_2_node));
  or or_1 (or_1_out, nor_1_out[0], Block);
  assign or_2_out = nor_1_out | {9{1'b0}};  // OR_Gate or_2, 9 bits wide
  or or_3 (or_3_out, pull_resistor_2_node[2], or_11_out);
  assign or_4_out = pull_resistor_2_node | or_9_out;  // OR_Gate or_4, 9 bits wide
  Pull_Resistor pull_resistor_3 (.node(pull_resistor_3_node));
  Pull_Resistor pull_resistor_4 (.node(pull_resistor_4_node));
  nor nor_3 (pull_resistor_3_node[4], nP1[0], nP1[6], nEmpty[4], or_1_out);
  assign or_5_out = pull_resistor_3_node | or_2_out;  // OR_Gate or_5, 9 bits wide
  nor nor_4 (pull_resistor_4_node[4], nP1[2], nP1[8], nEmpty[4], or_3_out);
  assign or_6_out = pull_resistor_4_node | or_4_out;  // OR_Gate or_6, 9 bits wide
  or or_7 (or_7_out, pull_resistor_3_node[4], or_1_out);
  or or_8 (or_8_out, pull_resistor_4_node[4], or_3_out);
  nor nor_5 (pull_resistor_5_node[8], nP1[0], nP1[4], nEmpty[8], or_7_out);
  Pull_Resistor pull_resistor_5 (.node(pull_resistor_5_node));
  assign or_9_out = pull_resistor_5_node | or_5_out;  // OR_Gate or_9, 9 bits wide
  nor nor_6 (pull_resistor_6_node[6], nP1[2], nP1[4], nEmpty[6], or_8_out);
  Pull_Resistor pull_resistor_6 (.node(pull_resistor_6_node));
  assign Move = pull_resistor_6_node | or_6_out;  // OR_Gate or_10, 9 bits wide
  or or_11 (or_11_out, pull_resistor_5_node[8], or_7_out);
  or or_12 (Block_2, pull_resistor_6_node[6], or_8_out);

  // Other names for the same wires on the sheet: E0 = nEmpty[0]; E1 = nEmpty[1]; E2 = nEmpty[2]; E3 = nEmpty[3];
  //   E4 = nEmpty[4]; E5 = nEmpty[5]; E6 = nEmpty[6]; E7 = nEmpty[7]; E8 = nEmpty[8]; A0 = nP1[0]; A1 = nP1[1];
  //   A2 = nP1[2]; A3 = nP1[3]; A4 = nP1[4]; A5 = nP1[5]; A6 = nP1[6]; A7 = nP1[7]; A8 = nP1[8]; B0 = nP2[0];
  //   B1 = nP2[1]; B2 = nP2[2]; B3 = nP2[3]; B4 = nP2[4]; B5 = nP2[5]; B6 = nP2[6]; B7 = nP2[7]; B8 = nP2[8]
endmodule

module CPU_Forks_Center (
  input  [8:0] nP1,
  input  Block,
  input  [8:0] nP2,
  input  [8:0] nEmpty,
  output Block_2,
  output [8:0] Move
);

  wire or_1_out, or_6_out, or_8_out;
  wire [8:0] or_2_out, or_5_out, or_7_out, pull_resistor_1_node, pull_resistor_2_node, pull_resistor_3_node,
       pull_resistor_4_node;

  nor nor_1 (pull_resistor_1_node[7], nP1[0], nP1[8], nEmpty[7], Block);
  Pull_Resistor pull_resistor_1 (.node(pull_resistor_1_node));
  nor nor_2 (pull_resistor_2_node[4], nEmpty[4], or_8_out);
  Pull_Resistor pull_resistor_2 (.node(pull_resistor_2_node));
  or or_1 (or_1_out, pull_resistor_1_node[7], Block);
  assign or_2_out = pull_resistor_1_node | {9{1'b0}};  // OR_Gate or_2, 9 bits wide
  or or_3 (Block_2, pull_resistor_2_node[4], or_8_out);
  assign Move = pull_resistor_2_node | or_7_out;  // OR_Gate or_4, 9 bits wide
  Pull_Resistor pull_resistor_3 (.node(pull_resistor_3_node));
  nor nor_3 (pull_resistor_3_node[7], nP1[2], nP1[6], nEmpty[7], or_1_out);
  assign or_5_out = pull_resistor_3_node | or_2_out;  // OR_Gate or_5, 9 bits wide
  or or_6 (or_6_out, pull_resistor_3_node[7], or_1_out);
  nor nor_4 (pull_resistor_4_node[8], nP1[5], nP1[7], nEmpty[8], or_6_out);
  Pull_Resistor pull_resistor_4 (.node(pull_resistor_4_node));
  assign or_7_out = pull_resistor_4_node | or_5_out;  // OR_Gate or_7, 9 bits wide
  or or_8 (or_8_out, pull_resistor_4_node[8], or_6_out);

  // Other names for the same wires on the sheet: E0 = nEmpty[0]; E1 = nEmpty[1]; E2 = nEmpty[2]; E3 = nEmpty[3];
  //   E4 = nEmpty[4]; E5 = nEmpty[5]; E6 = nEmpty[6]; E7 = nEmpty[7]; E8 = nEmpty[8]; A0 = nP1[0]; A1 = nP1[1];
  //   A2 = nP1[2]; A3 = nP1[3]; A4 = nP1[4]; A5 = nP1[5]; A6 = nP1[6]; A7 = nP1[7]; A8 = nP1[8]; B0 = nP2[0];
  //   B1 = nP2[1]; B2 = nP2[2]; B3 = nP2[3]; B4 = nP2[4]; B5 = nP2[5]; B6 = nP2[6]; B7 = nP2[7]; B8 = nP2[8]
endmodule

module CPU_Opposite_Corners (
  input  [8:0] nP1,
  input  [8:0] nP2,
  input  Block,
  input  [8:0] nEmpty,
  output Block_2,
  output [8:0] Move
);

  wire or_1_out, or_4_out, or_6_out;
  wire [8:0] nor_1_out, or_2_out, or_3_out, or_5_out, pull_resistor_2_node, pull_resistor_3_node,
       pull_resistor_4_node;

  nor nor_1 (nor_1_out[0], nP1[8], nEmpty[0], Block);
  Pull_Resistor pull_resistor_1 (.node(nor_1_out));
  or or_1 (or_1_out, nor_1_out[0], Block);
  assign or_2_out = nor_1_out | {9{1'b0}};  // OR_Gate or_2, 9 bits wide
  Pull_Resistor pull_resistor_2 (.node(pull_resistor_2_node));
  nor nor_2 (pull_resistor_2_node[8], nP1[0], nEmpty[8], or_1_out);
  assign or_3_out = pull_resistor_2_node | or_2_out;  // OR_Gate or_3, 9 bits wide
  or or_4 (or_4_out, pull_resistor_2_node[8], or_1_out);
  nor nor_3 (pull_resistor_3_node[2], nP1[6], nEmpty[2], or_4_out);
  Pull_Resistor pull_resistor_3 (.node(pull_resistor_3_node));
  assign or_5_out = pull_resistor_3_node | or_3_out;  // OR_Gate or_5, 9 bits wide
  or or_6 (or_6_out, pull_resistor_3_node[2], or_4_out);
  Pull_Resistor pull_resistor_4 (.node(pull_resistor_4_node));
  nor nor_4 (pull_resistor_4_node[6], nP1[2], nEmpty[6], or_6_out);
  or or_7 (Block_2, pull_resistor_4_node[6], or_6_out);
  assign Move = pull_resistor_4_node | or_5_out;  // OR_Gate or_8, 9 bits wide

  // Other names for the same wires on the sheet: E0 = nEmpty[0]; E1 = nEmpty[1]; E2 = nEmpty[2]; E3 = nEmpty[3];
  //   E4 = nEmpty[4]; E5 = nEmpty[5]; E6 = nEmpty[6]; E7 = nEmpty[7]; E8 = nEmpty[8]; A0 = nP1[0]; A1 = nP1[1];
  //   A2 = nP1[2]; A3 = nP1[3]; A4 = nP1[4]; A5 = nP1[5]; A6 = nP1[6]; A7 = nP1[7]; A8 = nP1[8]; B0 = nP2[0];
  //   B1 = nP2[1]; B2 = nP2[2]; B3 = nP2[3]; B4 = nP2[4]; B5 = nP2[5]; B6 = nP2[6]; B7 = nP2[7]; B8 = nP2[8]
endmodule

module CPU_Empty_Corner (
  input  [8:0] nP1,
  input  [8:0] nP2,
  input  Block,
  input  [8:0] nEmpty,
  output Block_2,
  output [8:0] Move
);

  wire or_1_out, or_4_out, or_6_out;
  wire [8:0] nor_1_out, or_2_out, or_3_out, or_5_out, pull_resistor_2_node, pull_resistor_3_node,
       pull_resistor_4_node;

  nor nor_1 (nor_1_out[0], nEmpty[0], Block);
  Pull_Resistor pull_resistor_1 (.node(nor_1_out));
  or or_1 (or_1_out, nor_1_out[0], Block);
  assign or_2_out = nor_1_out | {9{1'b0}};  // OR_Gate or_2, 9 bits wide
  Pull_Resistor pull_resistor_2 (.node(pull_resistor_2_node));
  nor nor_2 (pull_resistor_2_node[8], nEmpty[8], or_1_out);
  assign or_3_out = pull_resistor_2_node | or_2_out;  // OR_Gate or_3, 9 bits wide
  or or_4 (or_4_out, pull_resistor_2_node[8], or_1_out);
  nor nor_3 (pull_resistor_3_node[2], nEmpty[2], or_4_out);
  Pull_Resistor pull_resistor_3 (.node(pull_resistor_3_node));
  assign or_5_out = pull_resistor_3_node | or_3_out;  // OR_Gate or_5, 9 bits wide
  or or_6 (or_6_out, pull_resistor_3_node[2], or_4_out);
  Pull_Resistor pull_resistor_4 (.node(pull_resistor_4_node));
  nor nor_4 (pull_resistor_4_node[6], nEmpty[6], or_6_out);
  or or_7 (Block_2, pull_resistor_4_node[6], or_6_out);
  assign Move = pull_resistor_4_node | or_5_out;  // OR_Gate or_8, 9 bits wide

  // Other names for the same wires on the sheet: E0 = nEmpty[0]; E1 = nEmpty[1]; E2 = nEmpty[2]; E3 = nEmpty[3];
  //   E4 = nEmpty[4]; E5 = nEmpty[5]; E6 = nEmpty[6]; E7 = nEmpty[7]; E8 = nEmpty[8]; A0 = nP1[0]; A1 = nP1[1];
  //   A2 = nP1[2]; A3 = nP1[3]; A4 = nP1[4]; A5 = nP1[5]; A6 = nP1[6]; A7 = nP1[7]; A8 = nP1[8]; B0 = nP2[0];
  //   B1 = nP2[1]; B2 = nP2[2]; B3 = nP2[3]; B4 = nP2[4]; B5 = nP2[5]; B6 = nP2[6]; B7 = nP2[7]; B8 = nP2[8]
endmodule

module CPU_Empty_Side (
  input  [8:0] nP1,
  input  [8:0] nP2,
  input  Block,
  input  [8:0] nEmpty,
  output Block_2,
  output [8:0] Move
);

  wire or_1_out, or_4_out, or_6_out;
  wire [8:0] or_2_out, or_3_out, or_5_out, pull_resistor_1_node, pull_resistor_2_node, pull_resistor_3_node,
       pull_resistor_4_node;

  nor nor_1 (pull_resistor_1_node[1], nEmpty[1], Block);
  Pull_Resistor pull_resistor_1 (.node(pull_resistor_1_node));
  or or_1 (or_1_out, pull_resistor_1_node[1], Block);
  assign or_2_out = pull_resistor_1_node | {9{1'b0}};  // OR_Gate or_2, 9 bits wide
  Pull_Resistor pull_resistor_2 (.node(pull_resistor_2_node));
  nor nor_2 (pull_resistor_2_node[3], nEmpty[3], or_1_out);
  assign or_3_out = pull_resistor_2_node | or_2_out;  // OR_Gate or_3, 9 bits wide
  or or_4 (or_4_out, pull_resistor_2_node[3], or_1_out);
  nor nor_3 (pull_resistor_3_node[5], nEmpty[5], or_4_out);
  Pull_Resistor pull_resistor_3 (.node(pull_resistor_3_node));
  assign or_5_out = pull_resistor_3_node | or_3_out;  // OR_Gate or_5, 9 bits wide
  or or_6 (or_6_out, pull_resistor_3_node[5], or_4_out);
  Pull_Resistor pull_resistor_4 (.node(pull_resistor_4_node));
  nor nor_4 (pull_resistor_4_node[7], nP1[7], or_6_out);
  or or_7 (Block_2, pull_resistor_4_node[7], or_6_out);
  assign Move = pull_resistor_4_node | or_5_out;  // OR_Gate or_8, 9 bits wide

  // Other names for the same wires on the sheet: E0 = nEmpty[0]; E1 = nEmpty[1]; E2 = nEmpty[2]; E3 = nEmpty[3];
  //   E4 = nEmpty[4]; E5 = nEmpty[5]; E6 = nEmpty[6]; E7 = nEmpty[7]; E8 = nEmpty[8]; A0 = nP1[0]; A1 = nP1[1];
  //   A2 = nP1[2]; A3 = nP1[3]; A4 = nP1[4]; A5 = nP1[5]; A6 = nP1[6]; A7 = nP1[7]; A8 = nP1[8]; B0 = nP2[0];
  //   B1 = nP2[1]; B2 = nP2[2]; B3 = nP2[3]; B4 = nP2[4]; B5 = nP2[5]; B6 = nP2[6]; B7 = nP2[7]; B8 = nP2[8]
endmodule
